# Fritzing sketch sonometre (saved by Fritzing 0.9.3b)

parts:
  Composant1 = Arduino Nano (Rev3.0)
  BAT1 = Battery Holders [package=lipo-1100mAh]
  S1 = Toggle Switch [package=THT]
  Part1 = KY-037 High Sensitivity Sound Detection Module [package="Breakout board"]
  LED1 = smd LED [color="Red (633nm)" package="0805 [SMD]"]
  J1 = Piezo Speaker
  R1 = Resistor [tolerance=±5% resistance=220 package="2010 [SMD]"]

nets:
  N1: Composant1.GND, BAT1.-, Part1.G, R1.Pin_1
  N2: Composant1.D2, J1.pin2
  N3: Composant1.D3, LED1.anode
  N4: Composant1.D4, Part1.D0
  N5: Composant1.VIN, S1.L1
  N6: Composant1.3V3, Part1.+
  N7: BAT1.+, S1.COM

custom parts:
  KY-037 High Sensitivity Sound Detection Module: KY-037 high sensitivity sound detection module is an analog/digital sensor that uses a condenser microphone to observe changes in environment noise.
