# Fritzing sketch suiveur solaire (saved by Fritzing 0.9.3b)

parts:
  Composant1 = Arduino Uno (Rev3) - ICSP
  R1 = PHOTOCELL [package=photocell]
  R2 = PHOTOCELL [package=photocell]
  R3 = PHOTOCELL [package=photocell-kit]
  R4 = PHOTOCELL [package=photocell-kit]
  J1 = Basic Servo
  J2 = Basic Servo

nets:
  N1: Composant1.A0, R1.P$2, R3.P$1
  N2: Composant1.A1, R2.P$2, R4.P$1
  N3: Composant1.D9_PWM, J2.pulse
  N4: Composant1.D10_PWM/SS, J1.pulse
  GND: Composant1.GND, R1.P$1, R4.P$2, J1.gnd, J2.gnd
  VCC: Composant1.5V, R2.P$1, R3.P$2, J1.vcc, J2.vcc
